// Logisim project test.circ as structural Verilog: 3 circuits, main circuit 1b ALU
module _1b_ALU (
  input  SUB,
  input  C_IN,
  input  [2:0] in_3,
  input  A,
  input  B,
  input  LESS,
  output RESULT,
  output C_OUT,
  output SET
);

  wire and_1_out, nor_1_out, or_1_out, xor_1_out, xor_2_out;

  and and_1 (and_1_out, A, B);
  or or_1 (or_1_out, A, B);
  xor xor_1 (xor_1_out, A, B);
  nor nor_1 (nor_1_out, A, B);
  Adder #(.width(1)) adder_1 (.a(A), .b(xor_2_out), .out(SET), .cin(C_IN), .cout(C_OUT));
  xor xor_2 (xor_2_out, B, SUB);
  Multiplexer #(.select(3)) multiplexer_1 (
    .in0(and_1_out), .in1(or_1_out), .in2(xor_1_out), .in3(nor_1_out), .in4(SET), .in5(LESS), .out(RESULT),
    .sel(in_3));  // open: in6, in7, en

  // Notes on the sheet:
  //   OR
  //   XOR
  //   ADD/SUB
  //   ALU Operations
  //   AND
  //   NOR
endmodule

module ALU (
  input  [7:0] B,
  input  [7:0] A,
  input  SUB,
  input  [2:0] OP,
  output [7:0] R,
  output ZERO
);

  wire n1b_alu_1_c_out, n1b_alu_2_c_out, n1b_alu_3_c_out, n1b_alu_4_c_out, n1b_alu_5_c_out, n1b_alu_6_c_out,
       n1b_alu_7_c_out, n1b_alu_8_set;

  _1b_ALU u_1b_alu_1 (
    .A(A[0]), .B(B[0]), .RESULT(R[0]), .LESS(n1b_alu_8_set), .SUB(SUB), .C_IN(SUB), .in_3(OP),
    .C_OUT(n1b_alu_1_c_out));  // open: SET
  _1b_ALU u_1b_alu_2 (
    .A(A[1]), .B(B[1]), .RESULT(R[1]), .LESS(1'b0), .SUB(SUB), .C_IN(n1b_alu_1_c_out), .in_3(OP),
    .C_OUT(n1b_alu_2_c_out));  // open: SET
  _1b_ALU u_1b_alu_3 (
    .A(A[2]), .B(B[2]), .RESULT(R[2]), .LESS(1'b0), .SUB(SUB), .C_IN(n1b_alu_2_c_out), .in_3(OP),
    .C_OUT(n1b_alu_3_c_out));  // open: SET
  _1b_ALU u_1b_alu_4 (
    .A(A[3]), .B(B[3]), .RESULT(R[3]), .LESS(1'b0), .SUB(SUB), .C_IN(n1b_alu_3_c_out), .in_3(OP),
    .C_OUT(n1b_alu_4_c_out));  // open: SET
  _1b_ALU u_1b_alu_5 (
    .A(A[4]), .B(B[4]), .RESULT(R[4]), .LESS(1'b0), .SUB(SUB), .C_IN(n1b_alu_4_c_out), .in_3(OP),
    .C_OUT(n1b_alu_5_c_out));  // open: SET
  _1b_ALU u_1b_alu_6 (
    .A(A[5]), .B(B[5]), .RESULT(R[5]), .LESS(1'b0), .SUB(SUB), .C_IN(n1b_alu_5_c_out), .in_3(OP),
    .C_OUT(n1b_alu_6_c_out));  // open: SET
  _1b_ALU u_1b_alu_7 (
    .A(A[6]), .B(B[6]), .RESULT(R[6]), .LESS(1'b0), .SUB(SUB), .C_IN(n1b_alu_6_c_out), .in_3(OP),
    .C_OUT(n1b_alu_7_c_out));  // open: SET
  _1b_ALU u_1b_alu_8 (
    .A(A[7]), .B(B[7]), .RESULT(R[7]), .LESS(1'b0), .SUB(SUB), .C_IN(n1b_alu_7_c_out), .in_3(OP),
    .SET(n1b_alu_8_set));  // open: C_OUT
  nor nor_1 (ZERO, R[0], R[1], R[2], R[3], R[4], R[5], R[6], R[7]);
endmodule

module test (
  input  in_1,
  input  [2:0] in_2,
  input  [7:0] in_3,
  input  [7:0] in_4,
  output [7:0] out_5
);

  ALU alu_1 (.R(out_5), .B(in_4), .A(in_3), .SUB(in_1), .OP(in_2));  // open: ZERO
endmodule
