// Logisim project Ultimate ALU.circ as structural Verilog: 4 circuits, main circuit main
module main (
  input  [7:0] in_1,
  input  [7:0] in_2,
  input  [2:0] in_3
);

  wire [7:0] alu_1_out;
  wire [15:0] decimal_decoder_1_out_2, decimal_decoder_1_out_2_2;

  ALU alu_1 (.A(in_2), .B(in_1), .Out(alu_1_out), .OP(in_3));  // open: OE, Y
  Decimal_Decoder decimal_decoder_1 (.out_2({decimal_decoder_1_out_2_2, decimal_decoder_1_out_2}), .in_1(alu_1_out));
  _7_Segment_Display u_7_segment_display_1 (
    .g(decimal_decoder_1_out_2[15]), .f(decimal_decoder_1_out_2[14]), .a(decimal_decoder_1_out_2[13]),
    .b(decimal_decoder_1_out_2[12]), .e(decimal_decoder_1_out_2_2[15]), .d(decimal_decoder_1_out_2_2[14]),
    .c(decimal_decoder_1_out_2_2[13]), .dp(decimal_decoder_1_out_2_2[12]));
  _7_Segment_Display u_7_segment_display_2 (
    .g(decimal_decoder_1_out_2[11]), .f(decimal_decoder_1_out_2[10]), .a(decimal_decoder_1_out_2[9]),
    .b(decimal_decoder_1_out_2[8]), .e(decimal_decoder_1_out_2_2[11]), .d(decimal_decoder_1_out_2_2[10]),
    .c(decimal_decoder_1_out_2_2[9]), .dp(decimal_decoder_1_out_2_2[8]));
  _7_Segment_Display u_7_segment_display_3 (
    .g(decimal_decoder_1_out_2[7]), .f(decimal_decoder_1_out_2[6]), .a(decimal_decoder_1_out_2[5]),
    .b(decimal_decoder_1_out_2[4]), .e(decimal_decoder_1_out_2_2[7]), .d(decimal_decoder_1_out_2_2[6]),
    .c(decimal_decoder_1_out_2_2[5]), .dp(decimal_decoder_1_out_2_2[4]));
  _7_Segment_Display u_7_segment_display_4 (
    .g(decimal_decoder_1_out_2[3]), .f(decimal_decoder_1_out_2[2]), .a(decimal_decoder_1_out_2[1]),
    .b(decimal_decoder_1_out_2[0]), .e(decimal_decoder_1_out_2_2[3]), .d(decimal_decoder_1_out_2_2[2]),
    .c(decimal_decoder_1_out_2_2[1]), .dp(decimal_decoder_1_out_2_2[0]));
endmodule

module _8_Bit_Multiplier (
  input  [7:0] A,
  input  [7:0] B,
  output [15:0] out_3
);

  wire adder_1_cout, adder_2_cout, adder_2_out, adder_3_cout, adder_3_out, adder_4_cout, adder_4_out,
       adder_5_cout, adder_5_out, adder_6_cout, adder_6_out, adder_7_cout, adder_7_out, adder_8_cout,
       adder_8_out, adder_9_cout, adder_10_cout, adder_10_out, adder_11_cout, adder_11_out, adder_12_cout,
       adder_12_out, adder_13_cout, adder_13_out, adder_14_cout, adder_14_out, adder_15_cout, adder_15_out,
       adder_16_cout, adder_16_out, adder_17_cout, adder_18_cout, adder_18_out, adder_19_cout, adder_19_out,
       adder_20_cout, adder_20_out, adder_21_cout, adder_21_out, adder_22_cout, adder_22_out, adder_23_cout,
       adder_23_out, adder_24_cout, adder_24_out, adder_25_cout, adder_26_cout, adder_26_out, adder_27_cout,
       adder_27_out, adder_28_cout, adder_28_out, adder_29_cout, adder_29_out, adder_30_cout, adder_30_out,
       adder_31_cout, adder_31_out, adder_32_cout, adder_32_out, adder_33_cout, adder_34_cout, adder_34_out,
       adder_35_cout, adder_35_out, adder_36_out, adder_37_out, adder_38_out, adder_39_cout, adder_39_out,
       adder_40_cout, adder_40_out, adder_41_cout, adder_42_cout, adder_42_out, adder_43_cout, adder_43_out,
       adder_44_cout, adder_44_out, adder_45_cout, adder_45_out, adder_46_cout, adder_46_out, adder_47_cout,
       adder_47_out, adder_48_cout, adder_48_out, adder_55_cout, and_2_out, and_3_out, and_4_out, and_5_out,
       and_6_out, and_7_out, and_8_out, and_9_out, and_10_out, and_11_out, and_12_out, and_13_out,
       and_14_out, and_15_out, and_16_out, and_17_out, and_18_out, and_19_out, and_20_out, and_21_out,
       and_22_out, and_23_out, and_24_out, and_25_out, and_26_out, and_27_out, and_28_out, and_29_out,
       and_30_out, and_31_out, and_32_out, and_33_out, and_34_out, and_35_out, and_36_out, and_37_out,
       and_38_out, and_39_out, and_40_out, and_41_out, and_42_out, and_43_out, and_44_out, and_45_out,
       and_46_out, and_47_out, and_48_out, and_49_out, and_50_out, and_51_out, and_52_out, and_53_out,
       and_54_out, and_55_out, and_56_out, and_57_out, and_58_out, and_59_out, and_60_out, and_61_out,
       and_62_out, and_63_out, and_64_out;

  and and_1 (out_3[0], A[0], B[0]);
  and and_2 (and_2_out, A[1], B[0]);
  and and_3 (and_3_out, A[0], B[1]);
  and and_4 (and_4_out, A[2], B[0]);
  and and_5 (and_5_out, A[1], B[1]);
  and and_6 (and_6_out, A[3], B[0]);
  and and_7 (and_7_out, A[2], B[1]);
  and and_8 (and_8_out, A[4], B[0]);
  and and_9 (and_9_out, A[3], B[1]);
  and and_10 (and_10_out, A[5], B[0]);
  and and_11 (and_11_out, A[4], B[1]);
  and and_12 (and_12_out, A[6], B[0]);
  and and_13 (and_13_out, A[5], B[1]);
  and and_14 (and_14_out, A[7], B[0]);
  and and_15 (and_15_out, A[6], B[1]);
  and and_16 (and_16_out, A[7], B[1]);
  and and_17 (and_17_out, A[7], B[2]);
  and and_18 (and_18_out, A[7], B[3]);
  and and_19 (and_19_out, A[7], B[4]);
  and and_20 (and_20_out, A[7], B[5]);
  and and_21 (and_21_out, A[7], B[6]);
  and and_22 (and_22_out, A[7], B[7]);
  Adder #(.width(1)) adder_1 (.a(and_2_out), .b(and_3_out), .out(out_3[1]), .cin(1'b0), .cout(adder_1_cout));
  Adder #(.width(1)) adder_2 (.a(and_4_out), .b(and_5_out), .out(adder_2_out), .cin(adder_1_cout), .cout(adder_2_cout));
  Adder #(.width(1)) adder_3 (.a(and_6_out), .b(and_7_out), .out(adder_3_out), .cin(adder_2_cout), .cout(adder_3_cout));
  Adder #(.width(1)) adder_4 (.a(and_8_out), .b(and_9_out), .out(adder_4_out), .cin(adder_3_cout), .cout(adder_4_cout));
  Adder #(.width(1)) adder_5 (
    .a(and_10_out), .b(and_11_out), .out(adder_5_out), .cin(adder_4_cout), .cout(adder_5_cout));
  Adder #(.width(1)) adder_6 (
    .a(and_12_out), .b(and_13_out), .out(adder_6_out), .cin(adder_5_cout), .cout(adder_6_cout));
  Adder #(.width(1)) adder_7 (
    .a(and_14_out), .b(and_15_out), .out(adder_7_out), .cin(adder_6_cout), .cout(adder_7_cout));
  Adder #(.width(1)) adder_8 (.a(adder_7_cout), .b(and_16_out), .out(adder_8_out), .cin(1'b0), .cout(adder_8_cout));
  Adder #(.width(1)) adder_9 (.a(adder_2_out), .b(and_23_out), .out(out_3[2]), .cin(1'b0), .cout(adder_9_cout));
  and and_23 (and_23_out, A[0], B[2]);
  Adder #(.width(1)) adder_10 (
    .a(adder_3_out), .b(and_24_out), .out(adder_10_out), .cin(adder_9_cout), .cout(adder_10_cout));
  and and_24 (and_24_out, A[1], B[2]);
  Adder #(.width(1)) adder_11 (
    .a(adder_4_out), .b(and_25_out), .out(adder_11_out), .cin(adder_10_cout), .cout(adder_11_cout));
  and and_25 (and_25_out, A[2], B[2]);
  Adder #(.width(1)) adder_12 (
    .a(adder_5_out), .b(and_26_out), .out(adder_12_out), .cin(adder_11_cout), .cout(adder_12_cout));
  and and_26 (and_26_out, A[3], B[2]);
  Adder #(.width(1)) adder_13 (
    .a(adder_6_out), .b(and_27_out), .out(adder_13_out), .cin(adder_12_cout), .cout(adder_13_cout));
  and and_27 (and_27_out, A[4], B[2]);
  Adder #(.width(1)) adder_14 (
    .a(adder_7_out), .b(and_28_out), .out(adder_14_out), .cin(adder_13_cout), .cout(adder_14_cout));
  and and_28 (and_28_out, A[5], B[2]);
  Adder #(.width(1)) adder_15 (
    .a(adder_8_out), .b(and_29_out), .out(adder_15_out), .cin(adder_14_cout), .cout(adder_15_cout));
  and and_29 (and_29_out, A[6], B[2]);
  Adder #(.width(1)) adder_16 (
    .a(adder_8_cout), .b(and_17_out), .out(adder_16_out), .cin(adder_15_cout), .cout(adder_16_cout));
  and and_30 (and_30_out, A[0], B[3]);
  and and_31 (and_31_out, A[1], B[3]);
  and and_32 (and_32_out, A[2], B[3]);
  and and_33 (and_33_out, A[3], B[3]);
  and and_34 (and_34_out, A[4], B[3]);
  and and_35 (and_35_out, A[5], B[3]);
  and and_36 (and_36_out, A[6], B[3]);
  Adder #(.width(1)) adder_17 (.a(adder_10_out), .b(and_30_out), .out(out_3[3]), .cin(1'b0), .cout(adder_17_cout));
  Adder #(.width(1)) adder_18 (
    .a(adder_11_out), .b(and_31_out), .out(adder_18_out), .cin(adder_17_cout), .cout(adder_18_cout));
  and and_37 (and_37_out, A[0], B[4]);
  Adder #(.width(1)) adder_19 (
    .a(adder_12_out), .b(and_32_out), .out(adder_19_out), .cin(adder_18_cout), .cout(adder_19_cout));
  and and_38 (and_38_out, A[1], B[4]);
  Adder #(.width(1)) adder_20 (
    .a(adder_13_out), .b(and_33_out), .out(adder_20_out), .cin(adder_19_cout), .cout(adder_20_cout));
  and and_39 (and_39_out, A[2], B[4]);
  Adder #(.width(1)) adder_21 (
    .a(adder_14_out), .b(and_34_out), .out(adder_21_out), .cin(adder_20_cout), .cout(adder_21_cout));
  and and_40 (and_40_out, A[3], B[4]);
  Adder #(.width(1)) adder_22 (
    .a(adder_15_out), .b(and_35_out), .out(adder_22_out), .cin(adder_21_cout), .cout(adder_22_cout));
  and and_41 (and_41_out, A[4], B[4]);
  Adder #(.width(1)) adder_23 (
    .a(adder_16_out), .b(and_36_out), .out(adder_23_out), .cin(adder_22_cout), .cout(adder_23_cout));
  and and_42 (and_42_out, A[5], B[4]);
  Adder #(.width(1)) adder_24 (
    .a(adder_16_cout), .b(and_18_out), .out(adder_24_out), .cin(adder_23_cout), .cout(adder_24_cout));
  and and_43 (and_43_out, A[6], B[4]);
  Adder #(.width(1)) adder_25 (.a(adder_18_out), .b(and_37_out), .out(out_3[4]), .cin(1'b0), .cout(adder_25_cout));
  Adder #(.width(1)) adder_26 (
    .a(adder_19_out), .b(and_38_out), .out(adder_26_out), .cin(adder_25_cout), .cout(adder_26_cout));
  Adder #(.width(1)) adder_27 (
    .a(adder_20_out), .b(and_39_out), .out(adder_27_out), .cin(adder_26_cout), .cout(adder_27_cout));
  Adder #(.width(1)) adder_28 (
    .a(adder_21_out), .b(and_40_out), .out(adder_28_out), .cin(adder_27_cout), .cout(adder_28_cout));
  Adder #(.width(1)) adder_29 (
    .a(adder_22_out), .b(and_41_out), .out(adder_29_out), .cin(adder_28_cout), .cout(adder_29_cout));
  Adder #(.width(1)) adder_30 (
    .a(adder_23_out), .b(and_42_out), .out(adder_30_out), .cin(adder_29_cout), .cout(adder_30_cout));
  Adder #(.width(1)) adder_31 (
    .a(adder_24_out), .b(and_43_out), .out(adder_31_out), .cin(adder_30_cout), .cout(adder_31_cout));
  Adder #(.width(1)) adder_32 (
    .a(adder_24_cout), .b(and_19_out), .out(adder_32_out), .cin(adder_31_cout), .cout(adder_32_cout));
  Adder #(.width(1)) adder_33 (.a(adder_26_out), .b(and_44_out), .out(out_3[5]), .cin(1'b0), .cout(adder_33_cout));
  and and_44 (and_44_out, A[0], B[5]);
  Adder #(.width(1)) adder_34 (
    .a(adder_27_out), .b(and_45_out), .out(adder_34_out), .cin(adder_33_cout), .cout(adder_34_cout));
  and and_45 (and_45_out, A[1], B[5]);
  Adder #(.width(1)) adder_35 (
    .a(adder_28_out), .b(and_46_out), .out(adder_35_out), .cin(adder_34_cout), .cout(adder_35_cout));
  and and_46 (and_46_out, A[2], B[5]);
  Adder #(.width(1)) adder_36 (
    .a(adder_29_out), .b(and_47_out), .out(adder_36_out), .cin(adder_35_cout));  // open: cout
  and and_47 (and_47_out, A[3], B[5]);
  Adder #(.width(1)) adder_37 (.a(adder_30_out), .b(and_48_out), .out(adder_37_out));  // open: cin, cout
  and and_48 (and_48_out, A[4], B[5]);
  Adder #(.width(1)) adder_38 (.a(adder_31_out), .b(and_49_out), .out(adder_38_out));  // open: cin, cout
  and and_49 (and_49_out, A[5], B[5]);
  Adder #(.width(1)) adder_39 (
    .a(adder_32_out), .b(and_50_out), .out(adder_39_out), .cout(adder_39_cout));  // open: cin
  and and_50 (and_50_out, A[6], B[5]);
  Adder #(.width(1)) adder_40 (
    .a(adder_32_cout), .b(and_20_out), .out(adder_40_out), .cin(adder_39_cout), .cout(adder_40_cout));
  and and_51 (and_51_out, A[0], B[6]);
  and and_52 (and_52_out, A[1], B[6]);
  and and_53 (and_53_out, A[2], B[6]);
  and and_54 (and_54_out, A[3], B[6]);
  and and_55 (and_55_out, A[4], B[6]);
  and and_56 (and_56_out, A[5], B[6]);
  and and_57 (and_57_out, A[6], B[6]);
  Adder #(.width(1)) adder_41 (.a(adder_34_out), .b(and_51_out), .out(out_3[6]), .cin(1'b0), .cout(adder_41_cout));
  Adder #(.width(1)) adder_42 (
    .a(adder_35_out), .b(and_52_out), .out(adder_42_out), .cin(adder_41_cout), .cout(adder_42_cout));
  and and_58 (and_58_out, A[0], B[7]);
  Adder #(.width(1)) adder_43 (
    .a(adder_36_out), .b(and_53_out), .out(adder_43_out), .cin(adder_42_cout), .cout(adder_43_cout));
  and and_59 (and_59_out, A[1], B[7]);
  Adder #(.width(1)) adder_44 (
    .a(adder_37_out), .b(and_54_out), .out(adder_44_out), .cin(adder_43_cout), .cout(adder_44_cout));
  and and_60 (and_60_out, A[2], B[7]);
  Adder #(.width(1)) adder_45 (
    .a(adder_38_out), .b(and_55_out), .out(adder_45_out), .cin(adder_44_cout), .cout(adder_45_cout));
  and and_61 (and_61_out, A[3], B[7]);
  Adder #(.width(1)) adder_46 (
    .a(adder_39_out), .b(and_56_out), .out(adder_46_out), .cin(adder_45_cout), .cout(adder_46_cout));
  and and_62 (and_62_out, A[4], B[7]);
  Adder #(.width(1)) adder_47 (
    .a(adder_40_out), .b(and_57_out), .out(adder_47_out), .cin(adder_46_cout), .cout(adder_47_cout));
  and and_63 (and_63_out, A[5], B[7]);
  Adder #(.width(1)) adder_48 (
    .a(adder_40_cout), .b(and_21_out), .out(adder_48_out), .cin(adder_47_cout), .cout(adder_48_cout));
  and and_64 (and_64_out, A[6], B[7]);
  Adder #(.width(1)) adder_49 (.a(adder_42_out), .b(and_58_out), .out(out_3[7]), .cin(1'b0));  // open: cout
  Adder #(.width(1)) adder_50 (.a(adder_43_out), .b(and_59_out), .out(out_3[8]));  // open: cin, cout
  Adder #(.width(1)) adder_51 (.a(adder_44_out), .b(and_60_out), .out(out_3[9]));  // open: cin, cout
  Adder #(.width(1)) adder_52 (.a(adder_45_out), .b(and_61_out), .out(out_3[10]));  // open: cin, cout
  Adder #(.width(1)) adder_53 (.a(adder_46_out), .b(and_62_out), .out(out_3[11]));  // open: cin, cout
  Adder #(.width(1)) adder_54 (.a(adder_47_out), .b(and_63_out), .out(out_3[12]));  // open: cin, cout
  Adder #(.width(1)) adder_55 (.a(adder_48_out), .b(and_64_out), .out(out_3[13]), .cout(adder_55_cout));  // open: cin
  Adder #(.width(1)) adder_56 (
    .a(adder_48_cout), .b(and_22_out), .out(out_3[14]), .cin(adder_55_cout), .cout(out_3[15]));
endmodule

module ALU (
  input  [7:0] A,
  input  [7:0] B,
  input  OE,
  input  [2:0] OP,
  output [7:0] Y,
  output [7:0] Out
);

  wire [7:0] adder_1_out, and_1_out, bit_extender_1_out, divider_1_out, nor_1_out, or_1_out,
       subtractor_1_out, xor_1_out;
  wire [15:0] n8_bit_multiplier_1_out_3;

  assign and_1_out = A & B;  // AND_Gate and_1, 8 bits wide
  assign or_1_out = A | B;  // OR_Gate or_1, 8 bits wide
  assign nor_1_out = ~(A | B);  // NOR_Gate nor_1, 8 bits wide
  assign xor_1_out = A ^ B;  // XOR_Gate xor_1, 8 bits wide
  Adder adder_1 (.a(A), .b(B), .out(adder_1_out));  // open: cin, cout
  _8_Bit_Multiplier u_8_bit_multiplier_1 (.A(A), .B(B), .out_3(n8_bit_multiplier_1_out_3));
  Subtractor subtractor_1 (.a(A), .b(B), .out(subtractor_1_out));  // open: bin, bout
  Divider divider_1 (.a(A), .b(B), .out(divider_1_out));  // open: upper, rem
  Bit_Extender #(.in_width(16), .out_width(8)) bit_extender_1 (
    .in(n8_bit_multiplier_1_out_3), .out(bit_extender_1_out));
  Multiplexer #(.select(3), .width(8)) multiplexer_1 (
    .in0(and_1_out), .in1(or_1_out), .in2(nor_1_out), .in3(xor_1_out), .in4(adder_1_out),
    .in5(bit_extender_1_out), .in6(subtractor_1_out), .in7(divider_1_out), .out(Out), .sel(OP));  // open: en
  assign Y = OE ? Out : 8'bz;  // Controlled_Buffer controlled_buffer_1
endmodule

module Decimal_Decoder (
  input  [7:0] in_1,
  output [31:0] out_2
);

  ROM #(.dataWidth(32)) rom_1 (
    .addr(in_1),
    .data({out_2[31:28], out_2[15:12], out_2[27:24], out_2[11:8], out_2[23:20], out_2[7:4], out_2[19:16], out_2[3:0]}));  // open: sel

  // Notes on the sheet:
  //   contents of rom_1 (hex, n*v repeats v):
  //   e7 21 cb 6b 2d 6e ee 23 ef 2f 21e7 2121 21cb 216b 212d 216e 21ee 2123 21ef 212f cbe7 cb21 cbcb cb6b
  //   cb2d cb6e cbee cb23 cbef cb2f 6be7 6b21 6bcb 6b6b 6b2d 6b6e 6bee 6b23 6bef 6b2f 2de7 2d21 2dcb 2d6b
  //   2d2d 2d6e 2dee 2d23 2def 2d2f 6ee7 6e21 6ecb 6e6b 6e2d 6e6e 6eee 6e23 6eef 6e2f eee7 ee21 eecb ee6b
  //   ee2d ee6e eeee ee23 eeef ee2f 23e7 2321 23cb 236b 232d 236e 23ee 2323 23ef 232f efe7 ef21 efcb ef6b
  //   ef2d ef6e efee ef23 efef ef2f 2fe7 2f21 2fcb 2f6b 2f2d 2f6e 2fee 2f23 2fef 2f2f 21e7e7 21e721 21e7cb
  //   21e76b 21e72d 21e76e 21e7ee 21e723 21e7ef 21e72f 2121e7 212121 2121cb 21216b 21212d 21216e 2121ee
  //   212123 2121ef 21212f 21cbe7 21cb21 21cbcb 21cb6b 21cb2d 21cb6e 21cbee 21cb23 21cbef 21cb2f 216be7
  //   216b21 216bcb 216b6b 216b2d 216b6e 216bee 216b23 216bef 216b2f 212de7 212d21 212dcb 212d6b 212d2d
  //   212d6e 212dee 212d23 212def 212d2f 216ee7 216e21 216ecb 216e6b 216e2d 216e6e 216eee 216e23 216eef
  //   216e2f 21eee7 21ee21 21eecb 21ee6b 21ee2d 21ee6e 21eeee 21ee23 21eeef 21ee2f 2123e7 212321 2123cb
  //   21236b 21232d 21236e 2123ee 212323 2123ef 21232f 21efe7 21ef21 21efcb 21ef6b 21ef2d 21ef6e 21efee
  //   21ef23 21efef 21ef2f 212fe7 212f21 212fcb 212f6b 212f2d 212f6e 212fee 212f23 212fef 212f2f cbe7e7
  //   cbe721 cbe7cb cbe76b cbe72d cbe76e cbe7ee cbe723 cbe7ef cbe72f cb21e7 cb2121 cb21cb cb216b cb212d
  //   cb216e cb21ee cb2123 cb21ef cb212f cbcbe7 cbcb21 cbcbcb cbcb6b cbcb2d cbcb6e cbcbee cbcb23 cbcbef
  //   cbcb2f cb6be7 cb6b21 cb6bcb cb6b6b cb6b2d cb6b6e cb6bee cb6b23 cb6bef cb6b2f cb2de7 cb2d21 cb2dcb
  //   cb2d6b cb2d2d cb2d6e cb2dee cb2d23 cb2def cb2d2f cb6ee7 cb6e21 cb6ecb cb6e6b cb6e2d cb6e6e
endmodule
